// Logisim project OSMAN.circ as structural Verilog: 16 circuits, main circuit OSMAN
module OSMAN (
);

  wire ALU_cf, ALU_nf, ALU_vf, ALU_zf, ALUIzv1, ALUIzv2, CLK, CMem, Dekoder_Adresa_outputsrc,
       Dekoder_Adresa_outputwe, Dekoder_Adresa_ramoe, Dekoder_Adresa_ramwe, MemCLK, MemIzv, PMem, RST,
       RST_out, SkokReg, SR_cf, SR_nf, SR_vf, SR_zf, UpReg, UpStat;
  wire [1:0] Dekoder_Adresa_uiaddr, KJG_i, RegPod;
  wire [2:0] GranTip;
  wire [3:0] ALUOp, SW0_out;
  wire [7:0] ALU_i, MemorijaPodataka_dout, multiplexer_1_out, multiplexer_2_out, multiplexer_3_out,
       multiplexer_4_out, multiplexer_5_out, multiplexer_6_out, PB_dataout, PBInc,
       Predznaceno_Prosirenje_izlaz, RD_podacireg1, RD_podacireg2, UI_Kontroler_izlaz1, UI_Kontroler_izlaz2,
       UI_Kontroler_izlaz3, UI_Kontroler_izlaz4, UI_Kontroler_odabraniulaz, undriven;
  wire [15:0] InstrukcijskaMemorija_data;

  Clock #(.highDuration(2), .lowDuration(2)) u_CLK (.out(CLK));
  Clock #(.highDuration(2), .lowDuration(2), .phaseOffset(1)) u_MemCLK (.out(MemCLK));
  Button u_RST (.out(RST_out));
  D_Flip_Flop d_ff_1 (.D(RST_out), .clk(CLK), .Q(RST));  // open: Qn, preset, reset
  ProgramskiBrojac PB (.WE(1'b1), .Clock(CLK), .Reset(RST), .DataIn(multiplexer_2_out), .DataOut(PB_dataout));
  Sabirac PBSab (.A(8'h1), .B(PB_dataout), .Izlaz(PBInc));
  ROM #(.dataWidth(16)) InstrukcijskaMemorija (.addr(PB_dataout), .data(InstrukcijskaMemorija_data));
  KontrolnaJedinica KJ (
    .Opcode(InstrukcijskaMemorija_data[15:11]), .GranTip(GranTip), .SkokReg(SkokReg), .UpStat(UpStat),
    .CMem(CMem), .PMem(PMem), .ALUOp(ALUOp), .ALUIzv1(ALUIzv1), .ALUIzv2(ALUIzv2), .UpReg(UpReg),
    .RegPod(RegPod), .MemIzv(MemIzv));
  // Probe on InstrukcijskaMemorija_data[7:0]
  Multiplexer #(.select(2), .width(8)) multiplexer_1 (
    .in0(ALU_i), .in1(multiplexer_6_out), .in2(PBInc), .out(multiplexer_1_out), .sel(RegPod));  // open: in3
  Multiplexer #(.select(2), .width(8)) multiplexer_2 (
    .in0(PBInc), .in1(InstrukcijskaMemorija_data[7:0]), .in2(RD_podacireg1), .in3(RD_podacireg1),
    .out(multiplexer_2_out), .sel(KJG_i));
  RegistarskaDatoteka RD (
    .Reset(RST), .Clock(CLK), .UpReg(UpReg), .Reg1Adresa(InstrukcijskaMemorija_data[10:8]),
    .PodaciUpis(multiplexer_1_out), .Reg2Adresa(InstrukcijskaMemorija_data[7:5]), .PodaciReg1(RD_podacireg1),
    .PodaciReg2(RD_podacireg2));
  PredznacenoProsirenje Predznaceno_Prosirenje (
    .Ulaz(InstrukcijskaMemorija_data[4:0]), .Izlaz(Predznaceno_Prosirenje_izlaz));
  Multiplexer #(.width(8)) multiplexer_3 (
    .in0(RD_podacireg1), .in1(Predznaceno_Prosirenje_izlaz), .out(multiplexer_3_out), .sel(ALUIzv1));
  Multiplexer #(.width(8)) multiplexer_4 (
    .in0(RD_podacireg2), .in1(InstrukcijskaMemorija_data[7:0]), .out(multiplexer_4_out), .sel(ALUIzv2));
  KontrolnaJedinicaGrananja KJG (
    .SkokReg(SkokReg), .ZF(SR_zf), .NF(SR_nf), .VF(SR_vf), .CF(SR_cf), .GranTip(GranTip), .I(KJG_i));
  StatusniRegistar SR (
    .WE(UpStat), .Clock(CLK), .Reset(RST), .VFi(ALU_vf), .CFi(ALU_cf), .ZFi(ALU_zf), .NFi(ALU_nf),
    .VF(SR_vf), .CF(SR_cf), .ZF(SR_zf), .NF(SR_nf));
  ALU8Bit ALU (
    .ALUOp(ALUOp), .A(multiplexer_3_out), .B(multiplexer_4_out), .ZF(ALU_zf), .NF(ALU_nf), .VF(ALU_vf),
    .CF(ALU_cf), .I(ALU_i));
  // Probe on ALUOp
  // Probe on ALU_i
  Multiplexer #(.width(8)) multiplexer_5 (
    .in0(ALU_i), .in1(InstrukcijskaMemorija_data[7:0]), .out(multiplexer_5_out), .sel(MemIzv));
  Multiplexer #(.width(8)) multiplexer_6 (
    .in0(UI_Kontroler_odabraniulaz), .in1(MemorijaPodataka_dout), .out(multiplexer_6_out),
    .sel(Dekoder_Adresa_outputsrc));
  DekoderAdresa Dekoder_Adresa (
    .PMem(PMem), .CMem(CMem), .Addr(multiplexer_5_out), .OutputSrc(Dekoder_Adresa_outputsrc),
    .RAMWe(Dekoder_Adresa_ramwe), .RAMOe(Dekoder_Adresa_ramoe), .UIAddr(Dekoder_Adresa_uiaddr),
    .OutputWe(Dekoder_Adresa_outputwe));
  UIKontroler UI_Kontroler (
    .Clock(CLK), .WE(Dekoder_Adresa_outputwe), .RST(RST), .Adresa(Dekoder_Adresa_uiaddr), .Ulaz1(undriven),
    .Ulaz2({4'b0000, SW0_out}), .IzlazniPodaci(RD_podacireg1), .Izlaz1(UI_Kontroler_izlaz1),
    .Izlaz2(UI_Kontroler_izlaz2), .Izlaz3(UI_Kontroler_izlaz3), .Izlaz4(UI_Kontroler_izlaz4),
    .OdabraniUlaz(UI_Kontroler_odabraniulaz));  // open: Ulaz3, Ulaz4
  RAM #(.trigger("falling")) MemorijaPodataka (
    .addr(multiplexer_5_out), .we(Dekoder_Adresa_ramwe), .oe(Dekoder_Adresa_ramoe), .clk(MemCLK),
    .din(RD_podacireg1), .dout(MemorijaPodataka_dout));
  SevenSegAdapter SedSeg3 (.Segmenti(UI_Kontroler_izlaz1));
  SevenSegAdapter SedSeg2 (.Segmenti(UI_Kontroler_izlaz2));
  LED LED1 (.in(UI_Kontroler_izlaz4[7]));
  LED LED2 (.in(UI_Kontroler_izlaz4[6]));
  LED LED3 (.in(UI_Kontroler_izlaz4[5]));
  LED LED4 (.in(UI_Kontroler_izlaz4[4]));
  LED LED5 (.in(UI_Kontroler_izlaz4[3]));
  LED LED6 (.in(UI_Kontroler_izlaz4[2]));
  LED LED7 (.in(UI_Kontroler_izlaz4[1]));
  _7_Segment_Display SedSeg1 (
    .g(UI_Kontroler_izlaz3[6]), .f(UI_Kontroler_izlaz3[5]), .a(UI_Kontroler_izlaz3[0]),
    .b(UI_Kontroler_izlaz3[1]), .e(UI_Kontroler_izlaz3[4]), .d(UI_Kontroler_izlaz3[3]),
    .c(UI_Kontroler_izlaz3[2]), .dp(UI_Kontroler_izlaz3[7]));
  LED LED8 (.in(UI_Kontroler_izlaz4[0]));
  // DipSwitch DIP_Switch: pin names not known
  Button SW0 (.out(SW0_out[0]));
  Button SW1 (.out(SW0_out[1]));
  Button SW2 (.out(SW0_out[2]));
  Button SW3 (.out(SW0_out[3]));

  // Notes on the sheet:
  //   contents of InstrukcijskaMemorija (hex, n*v repeats v):
  //   90f7 910b 5001 d900 7715 4801 f9c0 8971 9172 5001 d900 9175 5001 d900 8171 5001 d900 7753 4803 f9c0
  //   9f14 5001 df00 5001 dd00 fd00 d1a2 5001 d900 9101 fa20 d100 4801 ea20 bf25 9100 9f26 9101 f100 a72b
  //   d1a2 fe20 9f4d d1a2 5001 d900 9101 fa20 d100 4801 1140 5001 d900 7715 4801 f9c0 5001 d900 d1a2 5001
  //   d900 9102 fa20 d100 4801 1140 5001 d900 7715 4801 f9c0 fa20 d100 4801 940 fe20 9f4d f8a0 d500 4801
  //   d700 4801 7f00 5001 df00 5001 dd00 fd00 5005 d1a2 d9ff 9100 d9fe d1fe 5001 d900 9103 fa20 d100 4801
  //   e940 b768 9100 9f69 9101 f100 a7a8 9100 d9fd d1ff 5001 d900 910a fa20 d100 4801 e940 bf78 9100 9f79
  //   9101 f100 a78e d1ff 5001 d900 910a fa20 d100 4801 1140 d9ff d1fd 5001 d900 9101 fa20 d100 4801 940
  //   d9fd 9f6d d1ff d9fc d1fc fa20 d3a3 b40 d160 d9fb d1fb 5001 d900 d1fe fa20 d3a4 b40 d160 fb20 d100
  //   4801 d960 d1fd d9ff d1fe 4901 d9fe 9f5d f8a0 d500 4801 d700 4801 7f00
endmodule

module FullAdder (
  input  A,
  input  B,
  input  Cin,
  output S,
  output Cout
);

  wire and_1_out, and_2_out, xor_1_out;

  xor xor_1 (xor_1_out, A, B);
  xor xor_2 (S, xor_1_out, Cin);
  and and_1 (and_1_out, xor_1_out, Cin);
  or or_1 (Cout, and_1_out, and_2_out);
  and and_2 (and_2_out, A, B);
endmodule

module ALU1Bit (
  input  InvB,
  input  A,
  input  B,
  input  Cin,
  input  [2:0] F,
  output Cout,
  output O
);

  wire and_1_out, FullAdder_1_s, not_1_out, or_1_out, xor_1_out, xor_2_out;

  xor xor_1 (xor_1_out, InvB, B);
  and and_1 (and_1_out, A, B);
  or or_1 (or_1_out, A, B);
  FullAdder FullAdder_1 (.A(A), .B(xor_1_out), .Cin(Cin), .S(FullAdder_1_s), .Cout(Cout));
  xor xor_2 (xor_2_out, A, B);
  not not_1 (not_1_out, A);
  Multiplexer #(.select(3)) multiplexer_1 (
    .in0(A), .in1(not_1_out), .in2(FullAdder_1_s), .in3(FullAdder_1_s), .in4(and_1_out), .in5(or_1_out),
    .in6(xor_2_out), .in7(B), .out(O), .sel(F));
endmodule

module ALU8Bit (
  input  [7:0] A,
  input  [7:0] B,
  input  [3:0] ALUOp,
  output VF,
  output CF,
  output ZF,
  output NF,
  output [7:0] I
);

  wire ALU1Bit_2_cout, ALU1Bit_3_cout, ALU1Bit_4_cout, ALU1Bit_5_cout, ALU1Bit_6_cout, ALU1Bit_7_cout,
       ALU1Bit_8_cout, and_1_out, not_1_out;
  wire [6:0] ALU1Bit_8_o;

  // Probe on A
  // Probe on B
  xor xor_1 (VF, ALU1Bit_2_cout, CF);
  and and_1 (and_1_out, ALUOp[0], ALUOp[1], not_1_out);
  not not_1 (not_1_out, ALUOp[2]);
  nor nor_1 (ZF, NF, ALU1Bit_8_o[6], ALU1Bit_8_o[5], ALU1Bit_8_o[4], ALU1Bit_8_o[3], ALU1Bit_8_o[2], ALU1Bit_8_o[1], ALU1Bit_8_o[0]);
  ALU1Bit ALU1Bit_1 (.InvB(and_1_out), .F(ALUOp[2:0]), .A(A[7]), .B(B[7]), .Cin(ALU1Bit_2_cout), .O(NF), .Cout(CF));
  ALU1Bit ALU1Bit_2 (
    .InvB(and_1_out), .F(ALUOp[2:0]), .A(A[6]), .B(B[6]), .Cin(ALU1Bit_3_cout), .O(ALU1Bit_8_o[6]),
    .Cout(ALU1Bit_2_cout));
  // Probe on I
  Multiplexer #(.select(2), .width(8)) multiplexer_1 (
    .in0({NF, ALU1Bit_8_o}), .in1({NF, ALU1Bit_8_o}), .in2({1'b0, A[7:1]}), .in3({A[6:0], 1'b0}), .out(I),
    .sel({ALUOp[3], ALUOp[0]}));
  ALU1Bit ALU1Bit_3 (
    .InvB(and_1_out), .F(ALUOp[2:0]), .A(A[5]), .B(B[5]), .Cin(ALU1Bit_4_cout), .O(ALU1Bit_8_o[5]),
    .Cout(ALU1Bit_3_cout));
  ALU1Bit ALU1Bit_4 (
    .InvB(and_1_out), .F(ALUOp[2:0]), .A(A[4]), .B(B[4]), .Cin(ALU1Bit_5_cout), .O(ALU1Bit_8_o[4]),
    .Cout(ALU1Bit_4_cout));
  ALU1Bit ALU1Bit_5 (
    .InvB(and_1_out), .F(ALUOp[2:0]), .A(A[3]), .B(B[3]), .Cin(ALU1Bit_6_cout), .O(ALU1Bit_8_o[3]),
    .Cout(ALU1Bit_5_cout));
  ALU1Bit ALU1Bit_6 (
    .InvB(and_1_out), .F(ALUOp[2:0]), .A(A[2]), .B(B[2]), .Cin(ALU1Bit_7_cout), .O(ALU1Bit_8_o[2]),
    .Cout(ALU1Bit_6_cout));
  ALU1Bit ALU1Bit_7 (
    .InvB(and_1_out), .F(ALUOp[2:0]), .A(A[1]), .B(B[1]), .Cin(ALU1Bit_8_cout), .O(ALU1Bit_8_o[1]),
    .Cout(ALU1Bit_7_cout));
  ALU1Bit ALU1Bit_8 (
    .InvB(and_1_out), .F(ALUOp[2:0]), .A(A[0]), .B(B[0]), .Cin(and_1_out), .O(ALU1Bit_8_o[0]),
    .Cout(ALU1Bit_8_cout));

  // Notes on the sheet:
  //   SR
  //   SL
  //   SUB
endmodule

module Registar8Bit (
  input  [7:0] DataIn,
  input  WE,
  input  Clock,
  input  Reset,
  output [7:0] DataOut
);

  wire multiplexer_1_out, multiplexer_2_out, multiplexer_3_out, multiplexer_4_out, multiplexer_5_out,
       multiplexer_6_out, multiplexer_7_out, multiplexer_8_out, not_1_out;

  not not_1 (not_1_out, WE);
  Multiplexer multiplexer_1 (.in0(DataIn[7]), .in1(DataOut[7]), .out(multiplexer_1_out), .sel(not_1_out));
  D_Flip_Flop #(.trigger("falling")) d_ff_1 (
    .D(multiplexer_1_out), .clk(Clock), .Q(DataOut[7]), .reset(Reset));  // open: Qn, preset
  Multiplexer multiplexer_2 (.in0(DataIn[6]), .in1(DataOut[6]), .out(multiplexer_2_out), .sel(not_1_out));
  D_Flip_Flop #(.trigger("falling")) d_ff_2 (
    .D(multiplexer_2_out), .clk(Clock), .Q(DataOut[6]), .reset(Reset));  // open: Qn, preset
  Multiplexer multiplexer_3 (.in0(DataIn[5]), .in1(DataOut[5]), .out(multiplexer_3_out), .sel(not_1_out));
  D_Flip_Flop #(.trigger("falling")) d_ff_3 (
    .D(multiplexer_3_out), .clk(Clock), .Q(DataOut[5]), .reset(Reset));  // open: Qn, preset
  Multiplexer multiplexer_4 (.in0(DataIn[4]), .in1(DataOut[4]), .out(multiplexer_4_out), .sel(not_1_out));
  D_Flip_Flop #(.trigger("falling")) d_ff_4 (
    .D(multiplexer_4_out), .clk(Clock), .Q(DataOut[4]), .reset(Reset));  // open: Qn, preset
  Multiplexer multiplexer_5 (.in0(DataIn[3]), .in1(DataOut[3]), .out(multiplexer_5_out), .sel(not_1_out));
  D_Flip_Flop #(.trigger("falling")) d_ff_5 (
    .D(multiplexer_5_out), .clk(Clock), .Q(DataOut[3]), .reset(Reset));  // open: Qn, preset
  Multiplexer multiplexer_6 (.in0(DataIn[2]), .in1(DataOut[2]), .out(multiplexer_6_out), .sel(not_1_out));
  D_Flip_Flop #(.trigger("falling")) d_ff_6 (
    .D(multiplexer_6_out), .clk(Clock), .Q(DataOut[2]), .reset(Reset));  // open: Qn, preset
  Multiplexer multiplexer_7 (.in0(DataIn[1]), .in1(DataOut[1]), .out(multiplexer_7_out), .sel(not_1_out));
  D_Flip_Flop #(.trigger("falling")) d_ff_7 (
    .D(multiplexer_7_out), .clk(Clock), .Q(DataOut[1]), .reset(Reset));  // open: Qn, preset
  Multiplexer multiplexer_8 (.in0(DataIn[0]), .in1(DataOut[0]), .out(multiplexer_8_out), .sel(not_1_out));
  D_Flip_Flop #(.trigger("falling")) d_ff_8 (
    .D(multiplexer_8_out), .clk(Clock), .Q(DataOut[0]), .reset(Reset));  // open: Qn, preset
endmodule

module RegistarskaDatoteka (
  input  [7:0] PodaciUpis,
  input  Clock,
  input  Reset,
  input  UpReg,
  input  [2:0] Reg1Adresa,
  input  [2:0] Reg2Adresa,
  output [7:0] PodaciReg1,
  output [7:0] PodaciReg2
);

  wire decoder_1_out0, decoder_1_out1, decoder_1_out2, decoder_1_out3, decoder_1_out4, decoder_1_out5,
       decoder_1_out6, decoder_1_out7;
  wire [7:0] Registar8Bit_1_dataout, Registar8Bit_2_dataout, Registar8Bit_3_dataout, Registar8Bit_4_dataout,
       Registar8Bit_5_dataout, Registar8Bit_6_dataout, Registar8Bit_7_dataout, Registar8Bit_8_dataout;

  Decoder #(.select(3)) decoder_1 (
    .out0(decoder_1_out0), .out1(decoder_1_out1), .out2(decoder_1_out2), .out3(decoder_1_out3),
    .out4(decoder_1_out4), .out5(decoder_1_out5), .out6(decoder_1_out6), .out7(decoder_1_out7),
    .sel(Reg1Adresa), .en(UpReg));
  Registar8Bit Registar8Bit_1 (
    .WE(decoder_1_out0), .Clock(Clock), .Reset(Reset), .DataIn(PodaciUpis), .DataOut(Registar8Bit_1_dataout));
  Registar8Bit Registar8Bit_2 (
    .WE(decoder_1_out1), .Clock(Clock), .Reset(Reset), .DataIn(PodaciUpis), .DataOut(Registar8Bit_2_dataout));
  Registar8Bit Registar8Bit_3 (
    .WE(decoder_1_out2), .Clock(Clock), .Reset(Reset), .DataIn(PodaciUpis), .DataOut(Registar8Bit_3_dataout));
  Registar8Bit Registar8Bit_4 (
    .WE(decoder_1_out3), .Clock(Clock), .Reset(Reset), .DataIn(PodaciUpis), .DataOut(Registar8Bit_4_dataout));
  Registar8Bit Registar8Bit_5 (
    .WE(decoder_1_out4), .Clock(Clock), .Reset(Reset), .DataIn(PodaciUpis), .DataOut(Registar8Bit_5_dataout));
  Registar8Bit Registar8Bit_6 (
    .WE(decoder_1_out5), .Clock(Clock), .Reset(Reset), .DataIn(PodaciUpis), .DataOut(Registar8Bit_6_dataout));
  Registar8Bit Registar8Bit_7 (
    .WE(decoder_1_out6), .Clock(Clock), .Reset(Reset), .DataIn(PodaciUpis), .DataOut(Registar8Bit_7_dataout));
  Registar8Bit Registar8Bit_8 (
    .WE(decoder_1_out7), .Clock(Clock), .Reset(Reset), .DataIn(PodaciUpis), .DataOut(Registar8Bit_8_dataout));
  Multiplexer #(.select(3), .width(8)) multiplexer_1 (
    .in0(Registar8Bit_1_dataout), .in1(Registar8Bit_2_dataout), .in2(Registar8Bit_3_dataout),
    .in3(Registar8Bit_4_dataout), .in4(Registar8Bit_5_dataout), .in5(Registar8Bit_6_dataout),
    .in6(Registar8Bit_7_dataout), .in7(Registar8Bit_8_dataout), .out(PodaciReg1), .sel(Reg1Adresa));
  Multiplexer #(.select(3), .width(8)) multiplexer_2 (
    .in0(Registar8Bit_1_dataout), .in1(Registar8Bit_2_dataout), .in2(Registar8Bit_3_dataout),
    .in3(Registar8Bit_4_dataout), .in4(Registar8Bit_5_dataout), .in5(Registar8Bit_6_dataout),
    .in6(Registar8Bit_7_dataout), .in7(Registar8Bit_8_dataout), .out(PodaciReg2), .sel(Reg2Adresa));

  // Notes on the sheet:
  //   SP
  //   A
  //   B
  //   C
  //   D
  //   E
  //   PV
  //   PA
endmodule

module ProgramskiBrojac (
  input  [7:0] DataIn,
  input  WE,
  input  Clock,
  input  Reset,
  output [7:0] DataOut
);

  wire multiplexer_1_out, multiplexer_2_out, multiplexer_3_out, multiplexer_4_out, multiplexer_5_out,
       multiplexer_6_out, multiplexer_7_out, multiplexer_8_out, not_1_out;

  not not_1 (not_1_out, WE);
  Multiplexer multiplexer_1 (.in0(DataIn[7]), .in1(DataOut[7]), .out(multiplexer_1_out), .sel(not_1_out));
  D_Flip_Flop d_ff_1 (.D(multiplexer_1_out), .clk(Clock), .Q(DataOut[7]), .reset(Reset));  // open: Qn, preset
  Multiplexer multiplexer_2 (.in0(DataIn[6]), .in1(DataOut[6]), .out(multiplexer_2_out), .sel(not_1_out));
  D_Flip_Flop d_ff_2 (.D(multiplexer_2_out), .clk(Clock), .Q(DataOut[6]), .reset(Reset));  // open: Qn, preset
  Multiplexer multiplexer_3 (.in0(DataIn[5]), .in1(DataOut[5]), .out(multiplexer_3_out), .sel(not_1_out));
  D_Flip_Flop d_ff_3 (.D(multiplexer_3_out), .clk(Clock), .Q(DataOut[5]), .reset(Reset));  // open: Qn, preset
  Multiplexer multiplexer_4 (.in0(DataIn[4]), .in1(DataOut[4]), .out(multiplexer_4_out), .sel(not_1_out));
  D_Flip_Flop d_ff_4 (.D(multiplexer_4_out), .clk(Clock), .Q(DataOut[4]), .reset(Reset));  // open: Qn, preset
  Multiplexer multiplexer_5 (.in0(DataIn[3]), .in1(DataOut[3]), .out(multiplexer_5_out), .sel(not_1_out));
  D_Flip_Flop d_ff_5 (.D(multiplexer_5_out), .clk(Clock), .Q(DataOut[3]), .reset(Reset));  // open: Qn, preset
  Multiplexer multiplexer_6 (.in0(DataIn[2]), .in1(DataOut[2]), .out(multiplexer_6_out), .sel(not_1_out));
  D_Flip_Flop d_ff_6 (.D(multiplexer_6_out), .clk(Clock), .Q(DataOut[2]), .reset(Reset));  // open: Qn, preset
  Multiplexer multiplexer_7 (.in0(DataIn[1]), .in1(DataOut[1]), .out(multiplexer_7_out), .sel(not_1_out));
  D_Flip_Flop d_ff_7 (.D(multiplexer_7_out), .clk(Clock), .Q(DataOut[1]), .reset(Reset));  // open: Qn, preset
  Multiplexer multiplexer_8 (.in0(DataIn[0]), .in1(DataOut[0]), .out(multiplexer_8_out), .sel(not_1_out));
  D_Flip_Flop d_ff_8 (.D(multiplexer_8_out), .clk(Clock), .Q(DataOut[0]), .reset(Reset));  // open: Qn, preset
endmodule

module StatusniRegistar (
  input  VFi,
  input  CFi,
  input  ZFi,
  input  NFi,
  input  WE,
  input  Clock,
  input  Reset,
  output VF,
  output CF,
  output ZF,
  output NF
);

  wire multiplexer_1_out, multiplexer_2_out, multiplexer_3_out, multiplexer_4_out, not_1_out;

  not not_1 (not_1_out, WE);
  Multiplexer multiplexer_1 (.in0(VFi), .in1(VF), .out(multiplexer_1_out), .sel(not_1_out));
  D_Flip_Flop #(.trigger("falling")) d_ff_1 (
    .D(multiplexer_1_out), .clk(Clock), .Q(VF), .reset(Reset));  // open: Qn, preset
  Multiplexer multiplexer_2 (.in0(CFi), .in1(CF), .out(multiplexer_2_out), .sel(not_1_out));
  D_Flip_Flop #(.trigger("falling")) d_ff_2 (
    .D(multiplexer_2_out), .clk(Clock), .Q(CF), .reset(Reset));  // open: Qn, preset
  Multiplexer multiplexer_3 (.in0(ZFi), .in1(ZF), .out(multiplexer_3_out), .sel(not_1_out));
  D_Flip_Flop #(.trigger("falling")) d_ff_3 (
    .D(multiplexer_3_out), .clk(Clock), .Q(ZF), .reset(Reset));  // open: Qn, preset
  Multiplexer multiplexer_4 (.in0(NFi), .in1(NF), .out(multiplexer_4_out), .sel(not_1_out));
  D_Flip_Flop #(.trigger("falling")) d_ff_4 (
    .D(multiplexer_4_out), .clk(Clock), .Q(NF), .reset(Reset));  // open: Qn, preset
endmodule

module KontrolnaJedinica (
  input  [4:0] Opcode,
  output UpStat,
  output ALUIzv1,
  output MemIzv,
  output [2:0] GranTip,
  output [1:0] RegPod,
  output [3:0] ALUOp,
  output UpReg,
  output CMem,
  output ALUIzv2,
  output SkokReg,
  output PMem
);

  ROM #(.addrWidth(5), .dataWidth(17)) KontrolniROM (
    .addr(Opcode),
    .data({GranTip, SkokReg, UpStat, CMem, PMem, ALUOp, ALUIzv1, ALUIzv2, UpReg, RegPod, MemIzv}));

  // Notes on the sheet:
  //   contents of KontrolniROM (hex, n*v repeats v):
  //   0 88 c8 48 108 148 188 208 248 98 d8 118 158 198 1c01c 2000 81b 413 1d8 1c010 4010 8010 c010 10010
  //   14010 18010 8aa 4a2 a8 10c0 10d0 1c8
endmodule

module PredznacenoProsirenje (
  input  [4:0] Ulaz,
  output [7:0] Izlaz
);


  assign Izlaz = {3'b000, Ulaz};
endmodule

module Sabirac (
  input  [7:0] A,
  input  [7:0] B,
  output [7:0] Izlaz
);

  wire FullAdder_2_cout, FullAdder_3_cout, FullAdder_4_cout, FullAdder_5_cout, FullAdder_6_cout,
       FullAdder_7_cout, FullAdder_8_cout;

  FullAdder FullAdder_1 (.A(A[7]), .B(B[7]), .Cin(FullAdder_2_cout), .S(Izlaz[7]));  // open: Cout
  FullAdder FullAdder_2 (.A(A[6]), .B(B[6]), .Cin(FullAdder_3_cout), .S(Izlaz[6]), .Cout(FullAdder_2_cout));
  FullAdder FullAdder_3 (.A(A[5]), .B(B[5]), .Cin(FullAdder_4_cout), .S(Izlaz[5]), .Cout(FullAdder_3_cout));
  FullAdder FullAdder_4 (.A(A[4]), .B(B[4]), .Cin(FullAdder_5_cout), .S(Izlaz[4]), .Cout(FullAdder_4_cout));
  FullAdder FullAdder_5 (.A(A[3]), .B(B[3]), .Cin(FullAdder_6_cout), .S(Izlaz[3]), .Cout(FullAdder_5_cout));
  FullAdder FullAdder_6 (.A(A[2]), .B(B[2]), .Cin(FullAdder_7_cout), .S(Izlaz[2]), .Cout(FullAdder_6_cout));
  FullAdder FullAdder_7 (.A(A[1]), .B(B[1]), .Cin(FullAdder_8_cout), .S(Izlaz[1]), .Cout(FullAdder_7_cout));
  FullAdder FullAdder_8 (.A(A[0]), .B(B[0]), .Cin(1'b0), .S(Izlaz[0]), .Cout(FullAdder_8_cout));

  // Notes on the sheet:
  //   Popraviti ovu shemu i razmisliti da se napravi da samo prima A i dodaje 1, umjesto da bude ovako pravi sabirac
endmodule

module KontrolnaJedinicaGrananja (
  input  SkokReg,
  input  [2:0] GranTip,
  input  ZF,
  input  NF,
  input  VF,
  input  CF,
  output [1:0] I
);

  wire not_1_out, not_2_out, not_3_out, xor_1_out;

  not not_1 (not_1_out, ZF);
  xor xor_1 (xor_1_out, NF, VF);
  not not_2 (not_2_out, CF);
  not not_3 (not_3_out, xor_1_out);
  Multiplexer #(.select(3)) multiplexer_1 (
    .in0(1'b0), .in1(ZF), .in2(not_1_out), .in3(xor_1_out), .in4(not_3_out), .in5(CF), .in6(not_2_out),
    .in7(1'b1), .out(I[0]), .sel(GranTip));

  assign I[1] = SkokReg;
endmodule

module DekoderAdresa (
  input  [7:0] Addr,
  input  PMem,
  input  CMem,
  output [1:0] UIAddr,
  output OutputWe,
  output RAMWe,
  output RAMOe,
  output OutputSrc
);

  wire and_3_out, not_1_out;

  Comparator #(.mode("unsigned")) comparator_1 (.a(8'hf8), .b(Addr), .gt(OutputSrc));  // open: eq, lt
  not not_1 (not_1_out, OutputSrc);
  and and_1 (RAMWe, OutputSrc, PMem);
  and and_2 (RAMOe, OutputSrc, CMem);
  and and_3 (and_3_out, not_1_out, Addr[2]);
  and and_4 (OutputWe, and_3_out, PMem);

  assign UIAddr = Addr[1:0];
endmodule

module StabilizatorUlaza8Bit (
  input  [7:0] DataIn,
  input  CLK,
  input  RST,
  output [7:0] DataOut
);

  D_Flip_Flop d_ff_1 (.D(DataIn[7]), .clk(CLK), .Q(DataOut[7]), .reset(RST));  // open: Qn, preset
  D_Flip_Flop d_ff_2 (.D(DataIn[6]), .clk(CLK), .Q(DataOut[6]), .reset(RST));  // open: Qn, preset
  D_Flip_Flop d_ff_3 (.D(DataIn[5]), .clk(CLK), .Q(DataOut[5]), .reset(RST));  // open: Qn, preset
  D_Flip_Flop d_ff_4 (.D(DataIn[4]), .clk(CLK), .Q(DataOut[4]), .reset(RST));  // open: Qn, preset
  D_Flip_Flop d_ff_5 (.D(DataIn[3]), .clk(CLK), .Q(DataOut[3]), .reset(RST));  // open: Qn, preset
  D_Flip_Flop d_ff_6 (.D(DataIn[2]), .clk(CLK), .Q(DataOut[2]), .reset(RST));  // open: Qn, preset
  D_Flip_Flop d_ff_7 (.D(DataIn[1]), .clk(CLK), .Q(DataOut[1]), .reset(RST));  // open: Qn, preset
  D_Flip_Flop d_ff_8 (.D(DataIn[0]), .clk(CLK), .Q(DataOut[0]), .reset(RST));  // open: Qn, preset
endmodule

module UIKontroler (
  input  RST,
  input  [7:0] IzlazniPodaci,
  input  Clock,
  input  WE,
  input  [1:0] Adresa,
  input  [7:0] Ulaz1,
  input  [7:0] Ulaz2,
  input  [7:0] Ulaz3,
  input  [7:0] Ulaz4,
  output [7:0] Izlaz1,
  output [7:0] Izlaz2,
  output [7:0] Izlaz3,
  output [7:0] Izlaz4,
  output [7:0] OdabraniUlaz
);

  wire decoder_1_out0, decoder_1_out1, decoder_1_out2, decoder_1_out3;
  wire [7:0] UIUlazniStabilizator1_dataout, UIUlazniStabilizator2_dataout, UIUlazniStabilizator3_dataout,
       UIUlazniStabilizator4_dataout;

  Decoder #(.select(2)) decoder_1 (
    .out0(decoder_1_out0), .out1(decoder_1_out1), .out2(decoder_1_out2), .out3(decoder_1_out3), .sel(Adresa),
    .en(WE));
  Registar8Bit UIIzlazniReg1 (
    .WE(decoder_1_out0), .Clock(Clock), .Reset(RST), .DataIn(IzlazniPodaci), .DataOut(Izlaz1));
  Registar8Bit UIIzlazniReg2 (
    .WE(decoder_1_out1), .Clock(Clock), .Reset(RST), .DataIn(IzlazniPodaci), .DataOut(Izlaz2));
  Registar8Bit UIIzlazniReg3 (
    .WE(decoder_1_out2), .Clock(Clock), .Reset(RST), .DataIn(IzlazniPodaci), .DataOut(Izlaz3));
  Registar8Bit UIIzlazniReg4 (
    .WE(decoder_1_out3), .Clock(Clock), .Reset(RST), .DataIn(IzlazniPodaci), .DataOut(Izlaz4));
  StabilizatorUlaza8Bit UIUlazniStabilizator1 (
    .CLK(Clock), .RST(RST), .DataIn(Ulaz1), .DataOut(UIUlazniStabilizator1_dataout));
  StabilizatorUlaza8Bit UIUlazniStabilizator2 (
    .CLK(Clock), .RST(RST), .DataIn(Ulaz2), .DataOut(UIUlazniStabilizator2_dataout));
  StabilizatorUlaza8Bit UIUlazniStabilizator3 (
    .CLK(Clock), .RST(RST), .DataIn(Ulaz3), .DataOut(UIUlazniStabilizator3_dataout));
  StabilizatorUlaza8Bit UIUlazniStabilizator4 (
    .CLK(Clock), .RST(RST), .DataIn(Ulaz4), .DataOut(UIUlazniStabilizator4_dataout));
  Multiplexer #(.select(2), .width(8)) multiplexer_1 (
    .in0(UIUlazniStabilizator1_dataout), .in1(UIUlazniStabilizator2_dataout),
    .in2(UIUlazniStabilizator3_dataout), .in3(UIUlazniStabilizator4_dataout), .out(OdabraniUlaz), .sel(Adresa));
endmodule

module SevenSegAdapter (
  input  [7:0] Segmenti
);

  _7_Segment_Display SedamSegDisplej (
    .g(Segmenti[6]), .f(Segmenti[5]), .a(Segmenti[0]), .b(Segmenti[1]), .e(Segmenti[4]), .d(Segmenti[3]),
    .c(Segmenti[2]), .dp(Segmenti[7]));
endmodule
